# Fritzing sketch LisaKeysPlus (saved by Fritzing 0.9.3b)
circuit board: 46.3cm x 11cm
breadboards: 1

parts:
  J1 = female pin header, 3 pins [form="♀ (female)"]
  LED1 = LED - 3mm [color="Red (633nm)" current=0.030 package="3 mm [THT]"]
  MX1 = Cherry MX Keyswitch Simple
  MX2 = Cherry MX Keyswitch Simple
  MX3 = Cherry MX Keyswitch Simple
  MX4 = Cherry MX Keyswitch Simple
  MX5 = Cherry MX Keyswitch Simple
  MX6 = Cherry MX Keyswitch Simple
  MX7 = Cherry MX Keyswitch Simple
  MX8 = Cherry MX Keyswitch Simple
  MX9 = Cherry MX Keyswitch Simple
  MX10 = Cherry MX Keyswitch Simple
  MX11 = Cherry MX Keyswitch Simple
  MX12 = Cherry MX Keyswitch Simple
  MX13 = Cherry MX Keyswitch Simple
  MX14 = Cherry MX Keyswitch Simple
  MX15 = Cherry MX Keyswitch Simple
  MX16 = Cherry MX Keyswitch Simple
  MX17 = Cherry MX Keyswitch Simple
  MX18 = Cherry MX Keyswitch Simple
  MX19 = Cherry MX Keyswitch Simple
  MX20 = Cherry MX Keyswitch Simple
  MX21 = Cherry MX Keyswitch Simple
  MX22 = Cherry MX Keyswitch Simple
  MX23 = Cherry MX Keyswitch Simple
  MX24 = Cherry MX Keyswitch Simple
  MX25 = Cherry MX Keyswitch Simple
  MX26 = Cherry MX Keyswitch Simple
  MX27 = Cherry MX Keyswitch Simple
  MX28 = Cherry MX Keyswitch Simple
  MX29 = Cherry MX Keyswitch Simple
  MX30 = Cherry MX Keyswitch Simple
  MX31 = Cherry MX Keyswitch Simple
  MX32 = Cherry MX Keyswitch Simple
  MX33 = Cherry MX Keyswitch Simple
  MX34 = Cherry MX Keyswitch Simple
  MX35 = Cherry MX Keyswitch Simple
  MX36 = Cherry MX Keyswitch Simple
  MX37 = Cherry MX Keyswitch Simple
  MX38 = Cherry MX Keyswitch Simple
  MX39 = Cherry MX Keyswitch Simple
  MX40 = Cherry MX Keyswitch Simple
  MX42 = Cherry MX Keyswitch Simple
  MX43 = Cherry MX Keyswitch Simple
  MX44 = Cherry MX Keyswitch Simple
  MX45 = Cherry MX Keyswitch Simple
  MX47 = Cherry MX Keyswitch Simple
  MX48 = Cherry MX Keyswitch Simple
  MX49 = Cherry MX Keyswitch Simple
  MX50 = Cherry MX Keyswitch Simple
  MX51 = Cherry MX Keyswitch Simple
  MX52 = Cherry MX Keyswitch Simple
  MX53 = Cherry MX Keyswitch Simple
  MX54 = Cherry MX Keyswitch Simple
  MX56 = Cherry MX Keyswitch Simple
  MX57 = Cherry MX Keyswitch Simple
  MX58 = Cherry MX Keyswitch Simple
  MX59 = Cherry MX Keyswitch Simple
  MX60 = Cherry MX Keyswitch Simple
  MX61 = Cherry MX Keyswitch Simple
  MX62 = Cherry MX Keyswitch Simple
  MX63 = Cherry MX Keyswitch Simple
  MX64 = Cherry MX Keyswitch Simple
  MX65 = Cherry MX Keyswitch Simple
  MX66 = Cherry MX Keyswitch Simple
  MX67 = Cherry MX Keyswitch Simple
  MX68 = Cherry MX Keyswitch Simple
  MX69 = Cherry MX Keyswitch Simple
  MX70 = Cherry MX Keyswitch Simple
  MX71 = Cherry MX Keyswitch Simple
  MX72 = Cherry MX Keyswitch Simple
  MX73 = Cherry MX Keyswitch Simple
  MX74 = Cherry MX Keyswitch Simple
  MX75 = Cherry MX Keyswitch Simple
  MX76 = Cherry MX Keyswitch Simple
  MX77 = Cherry MX Keyswitch Simple
  MX79 = Cherry MX Keyswitch Simple
  MX80 = Cherry MX Keyswitch Simple
  MX81 = Cherry MX Keyswitch Simple
  MX83 = Cherry MX Keyswitch Simple
  D1 = Rectifier Diode [part_number=1N4001 package="300 mil [THT]"]
  D2 = Rectifier Diode [part_number=1N4001 package="300 mil [THT]"]
  D3 = Rectifier Diode [part_number=1N4001 package="300 mil [THT]"]
  D4 = Rectifier Diode [part_number=1N4001 package="300 mil [THT]"]
  D5 = Rectifier Diode [part_number=1N4001 package="300 mil [THT]"]
  D6 = Rectifier Diode [part_number=1N4001 package="300 mil [THT]"]
  D7 = Rectifier Diode [part_number=1N4001 package="300 mil [THT]"]
  D8 = Rectifier Diode [part_number=1N4001 package="300 mil [THT]"]
  D9 = Rectifier Diode [part_number=1N4001 package="300 mil [THT]"]
  D10 = Rectifier Diode [part_number=1N4001 package="300 mil [THT]"]
  D11 = Rectifier Diode [part_number=1N4001 package="300 mil [THT]"]
  D12 = Rectifier Diode [part_number=1N4001 package="300 mil [THT]"]
  D13 = Rectifier Diode [part_number=1N4001 package="300 mil [THT]"]
  D14 = Rectifier Diode [part_number=1N4001 package="300 mil [THT]"]
  D15 = Rectifier Diode [part_number=1N4001 package="300 mil [THT]"]
  D16 = Rectifier Diode [part_number=1N4001 package="300 mil [THT]"]
  D17 = Rectifier Diode [part_number=1N4001 package="300 mil [THT]"]
  D18 = Rectifier Diode [part_number=1N4001 package="300 mil [THT]"]
  D19 = Rectifier Diode [part_number=1N4001 package="300 mil [THT]"]
  D20 = Rectifier Diode [part_number=1N4001 package="300 mil [THT]"]
  D21 = Rectifier Diode [part_number=1N4001 package="300 mil [THT]"]
  D22 = Rectifier Diode [part_number=1N4001 package="300 mil [THT]"]
  D23 = Rectifier Diode [part_number=1N4001 package="300 mil [THT]"]
  D24 = Rectifier Diode [part_number=1N4001 package="300 mil [THT]"]
  D25 = Rectifier Diode [part_number=1N4001 package="300 mil [THT]"]
  D26 = Rectifier Diode [part_number=1N4001 package="300 mil [THT]"]
  D27 = Rectifier Diode [part_number=1N4001 package="300 mil [THT]"]
  D28 = Rectifier Diode [part_number=1N4001 package="300 mil [THT]"]
  D29 = Rectifier Diode [part_number=1N4001 package="300 mil [THT]"]
  D30 = Rectifier Diode [part_number=1N4001 package="300 mil [THT]"]
  D31 = Rectifier Diode [part_number=1N4001 package="300 mil [THT]"]
  D33 = Rectifier Diode [part_number=1N4001 package="300 mil [THT]"]
  D34 = Rectifier Diode [part_number=1N4001 package="300 mil [THT]"]
  D35 = Rectifier Diode [part_number=1N4001 package="300 mil [THT]"]
  D36 = Rectifier Diode [part_number=1N4001 package="300 mil [THT]"]
  D37 = Rectifier Diode [part_number=1N4001 package="300 mil [THT]"]
  D38 = Rectifier Diode [part_number=1N4001 package="300 mil [THT]"]
  D39 = Rectifier Diode [part_number=1N4001 package="300 mil [THT]"]
  D40 = Rectifier Diode [part_number=1N4001 package="300 mil [THT]"]
  D41 = Rectifier Diode [part_number=1N4001 package="300 mil [THT]"]
  D42 = Rectifier Diode [part_number=1N4001 package="300 mil [THT]"]
  D43 = Rectifier Diode [part_number=1N4001 package="300 mil [THT]"]
  D44 = Rectifier Diode [part_number=1N4001 package="300 mil [THT]"]
  D45 = Rectifier Diode [part_number=1N4001 package="300 mil [THT]"]
  D47 = Rectifier Diode [part_number=1N4001 package="300 mil [THT]"]
  D48 = Rectifier Diode [part_number=1N4001 package="300 mil [THT]"]
  D49 = Rectifier Diode [part_number=1N4001 package="300 mil [THT]"]
  D51 = Rectifier Diode [part_number=1N4001 package="300 mil [THT]"]
  D52 = Rectifier Diode [part_number=1N4001 package="300 mil [THT]"]
  D53 = Rectifier Diode [part_number=1N4001 package="300 mil [THT]"]
  D54 = Rectifier Diode [part_number=1N4001 package="300 mil [THT]"]
  D55 = Rectifier Diode [part_number=1N4001 package="300 mil [THT]"]
  D56 = Rectifier Diode [part_number=1N4001 package="300 mil [THT]"]
  D57 = Rectifier Diode [part_number=1N4001 package="300 mil [THT]"]
  D58 = Rectifier Diode [part_number=1N4001 package="300 mil [THT]"]
  D59 = Rectifier Diode [part_number=1N4001 package="300 mil [THT]"]
  D60 = Rectifier Diode [part_number=1N4001 package="300 mil [THT]"]
  D61 = Rectifier Diode [part_number=1N4001 package="300 mil [THT]"]
  D62 = Rectifier Diode [part_number=1N4001 package="300 mil [THT]"]
  D63 = Rectifier Diode [part_number=1N4001 package="300 mil [THT]"]
  D64 = Rectifier Diode [part_number=1N4001 package="300 mil [THT]"]
  D65 = Rectifier Diode [part_number=1N4001 package="300 mil [THT]"]
  D66 = Rectifier Diode [part_number=1N4001 package="300 mil [THT]"]
  D67 = Rectifier Diode [part_number=1N4001 package="300 mil [THT]"]
  D68 = Rectifier Diode [part_number=1N4001 package="300 mil [THT]"]
  D69 = Rectifier Diode [part_number=1N4001 package="300 mil [THT]"]
  D70 = Rectifier Diode [part_number=1N4001 package="300 mil [THT]"]
  D71 = Rectifier Diode [part_number=1N4001 package="300 mil [THT]"]
  D72 = Rectifier Diode [part_number=1N4001 package="300 mil [THT]"]
  D73 = Rectifier Diode [part_number=1N4001 package="300 mil [THT]"]
  D74 = Rectifier Diode [part_number=1N4001 package="300 mil [THT]"]
  D75 = Rectifier Diode [part_number=1N4001 package="300 mil [THT]"]
  D76 = Rectifier Diode [part_number=1N4001 package="300 mil [THT]"]
  D77 = Rectifier Diode [part_number=1N4001 package="300 mil [THT]"]
  D78 = Rectifier Diode [part_number=1N4001 package="300 mil [THT]"]
  D79 = Rectifier Diode [part_number=1N4001 package="300 mil [THT]"]
  J2 = female pin header, 14 pins [form="♀ (female)"]
  J3 = female pin header, 14 pins [form="♀ (female)"]
  J4 = female pin header, 5 pins [form="♀ (female)"]
  J5 = female pin header, 3 pins [form="♀ (female)"]
  R1 = Resistor [tolerance=±5% power=0.25 resistance=220 package=THT]
  LED2 = LED - 3mm [color="Red (633nm)" current=0.030 package="3 mm [THT]"]
  LED3 = LED - 3mm [color="Red (633nm)" current=0.030 package="3 mm [THT]"]
  LED4 = LED - 3mm [color="Red (633nm)" current=0.030 package="3 mm [THT]"]
  LED5 = LED - 3mm [color="Red (633nm)" current=0.030 package="3 mm [THT]"]
  J6 = female pin header, 3 pins [form="♀ (female)"]  # not connected

nets:
  N1: J1.pin1, J5.pin2
  N2: J1.pin2, LED1.cathode, J3.pin2, J4.pin2, LED2.cathode, LED3.cathode, LED4.cathode, LED5.cathode
  N3: J1.pin3, J2.pin13
  N4: LED1.anode, R1.Pin_0, LED2.anode, LED3.anode, LED4.anode, LED5.anode
  N5: MX1.pin_1, D1.anode
  N6: MX1.pin_2, MX15.pin_2, MX29.pin_2, MX43.pin_2, MX67.pin_2, MX70.pin_2, MX74.pin_2, MX81.pin_2, J3.pin8
  N7: MX2.pin_1, D2.anode
  N8: MX2.pin_2, MX23.pin_2, MX37.pin_2, MX51.pin_2, MX66.pin_2, MX69.pin_2, MX73.pin_2, MX77.pin_2, J3.pin9
  N9: MX3.pin_1, D3.anode
  N10: MX3.pin_2, MX16.pin_2, MX30.pin_2, MX44.pin_2, MX65.pin_2, MX68.pin_2, MX72.pin_2, MX76.pin_2, J3.pin7
  N11: MX4.pin_1, D4.anode
  N12: MX4.pin_2, MX14.pin_2, MX21.pin_2, MX27.pin_2, MX35.pin_2, MX49.pin_2, MX80.pin_2, MX83.pin_2, J3.pin5
  N13: MX5.pin_1, D5.anode
  N14: MX5.pin_2, MX13.pin_2, MX18.pin_2, MX25.pin_2, MX32.pin_2, MX39.pin_2, MX53.pin_2, MX54.pin_2, J3.pin12
  N15: MX6.pin_1, D6.anode
  N16: MX6.pin_2, MX12.pin_2, MX24.pin_2, MX26.pin_2, MX38.pin_2, MX40.pin_2, MX52.pin_2, MX63.pin_2, J3.pin11
  N17: MX7.pin_1, D7.anode
  N18: MX7.pin_2, MX11.pin_2, MX20.pin_2, MX22.pin_2, MX34.pin_2, MX36.pin_2, MX48.pin_2, MX50.pin_2, J4.pin5
  N19: MX8.pin_1, D8.anode
  N20: MX8.pin_2, MX10.pin_2, MX17.pin_2, MX28.pin_2, MX31.pin_2, MX42.pin_2, MX45.pin_2, MX56.pin_2, J4.pin4
  N21: MX9.pin_1, D9.anode
  N22: MX9.pin_2, MX19.pin_2, MX33.pin_2, MX47.pin_2, J4.pin3
  N23: MX10.pin_1, D10.anode
  N24: MX11.pin_1, D11.anode
  N25: MX12.pin_1, D12.anode
  N26: MX13.pin_1, D13.anode
  N27: MX14.pin_1, D14.anode
  N28: MX15.pin_1, D15.anode
  N29: MX16.pin_1, D26.anode
  N30: MX17.pin_1, D25.anode
  N31: MX18.pin_1, D22.anode
  N32: MX19.pin_1, D17.anode
  N33: MX20.pin_1, D19.anode
  N34: MX21.pin_1, D20.anode
  N35: MX22.pin_1, D16.anode
  N36: MX23.pin_1, D27.anode
  N37: MX24.pin_1, D24.anode
  N38: MX25.pin_1, D28.anode
  N39: MX26.pin_1, D21.anode
  N40: MX27.pin_1, D18.anode
  N41: MX28.pin_1, D23.anode
  N42: MX29.pin_1, D29.anode
  N43: MX30.pin_1, D40.anode
  N44: MX31.pin_1, D39.anode
  N45: MX32.pin_1, D36.anode
  N46: MX33.pin_1, D31.anode
  N47: MX34.pin_1, D33.anode
  N48: MX35.pin_1, D34.anode
  N49: MX36.pin_1, D30.anode
  N50: MX37.pin_1, D41.anode
  N51: MX38.pin_1, D38.anode
  N52: MX39.pin_1, D42.anode
  N53: MX40.pin_1, D35.anode
  N54: MX42.pin_1, D37.anode
  N55: MX43.pin_1, D43.anode
  N56: MX44.pin_1, D54.anode
  N57: MX45.pin_1, D53.anode
  N58: MX47.pin_1, D45.anode
  N59: MX48.pin_1, D47.anode
  N60: MX49.pin_1, D48.anode
  N61: MX50.pin_1, D44.anode
  N62: MX51.pin_1, D55.anode
  N63: MX52.pin_1, D52.anode
  N64: MX53.pin_1, D56.anode
  N65: MX54.pin_1, D49.anode
  N66: MX56.pin_1, D51.anode
  N67: MX57.pin_1, D57.anode
  N68: MX57.pin_2, MX58.pin_2, MX59.pin_2, MX60.pin_2, MX61.pin_2, MX62.pin_2, MX64.pin_2, MX71.pin_2, MX75.pin_2, MX79.pin_2, J3.pin6
  N69: MX58.pin_1, D58.anode
  N70: MX59.pin_1, MX60.pin_1, MX61.pin_1, D59.anode
  N71: MX62.pin_1, D60.anode
  N72: MX63.pin_1, D61.anode
  N73: MX64.pin_1, D62.anode
  N74: MX65.pin_1, D63.anode
  N75: MX66.pin_1, D64.anode
  N76: MX67.pin_1, D65.anode
  N77: MX68.pin_1, D68.anode
  N78: MX69.pin_1, D67.anode
  N79: MX70.pin_1, D69.anode
  N80: MX71.pin_1, D66.anode
  N81: MX72.pin_1, D72.anode
  N82: MX73.pin_1, D71.anode
  N83: MX74.pin_1, D73.anode
  N84: MX75.pin_1, D70.anode
  N85: MX76.pin_1, D76.anode
  N86: MX77.pin_1, D75.anode
  N87: MX79.pin_1, D74.anode
  N88: MX80.pin_1, D79.anode
  N89: MX81.pin_1, D78.anode
  N90: MX83.pin_1, D77.anode
  N91: D1.cathode, D2.cathode, D3.cathode, D4.cathode, D5.cathode, D6.cathode, D7.cathode, D8.cathode, D9.cathode, D60.cathode, J2.pin6
  N92: D10.cathode, D11.cathode, D12.cathode, D13.cathode, D14.cathode, D62.cathode, D63.cathode, D64.cathode, D65.cathode, J2.pin5
  N93: D15.cathode, D17.cathode, D19.cathode, D20.cathode, D24.cathode, D25.cathode, D26.cathode, D27.cathode, D28.cathode, D59.cathode, J2.pin8
  N94: D16.cathode, D18.cathode, D21.cathode, D22.cathode, D23.cathode, D66.cathode, D67.cathode, D68.cathode, D69.cathode, J2.pin7
  N95: D29.cathode, D31.cathode, D33.cathode, D34.cathode, D38.cathode, D39.cathode, D40.cathode, D41.cathode, D42.cathode, D58.cathode, J2.pin10
  N96: D30.cathode, D35.cathode, D36.cathode, D37.cathode, D70.cathode, D71.cathode, D72.cathode, D73.cathode, D77.cathode, J2.pin9
  N97: D43.cathode, D45.cathode, D47.cathode, D48.cathode, D52.cathode, D53.cathode, D54.cathode, D55.cathode, D56.cathode, D57.cathode, J2.pin11
  N98: D44.cathode, D49.cathode, D51.cathode, D61.cathode, D74.cathode, D75.cathode, D76.cathode, D78.cathode, D79.cathode, J2.pin12
  N99: J2.pin2, J5.pin1
  N100: J3.pin1, J5.pin3
  N101: J3.pin4, R1.Pin_1

notes:
  BAT
  VCC
  TIP
  ItsyBitsy 32u4 5v
  150R
  Keyboard Replacement PCB
  Keys+
  github.com/RebeccaRGB/lisakeysplus
  VCC - TIP
  GND - SLEEVE
  DATA - RING
  Rev B

custom parts:
  Cherry MX Keyswitch Simple: Cherry MX Keyswitch button for keyboards
